// Logisim project cpu.circ as structural Verilog: 11 circuits, main circuit main
module main (
  input  reset
);

  wire ALUinB, and_1_out, and_2_out, beqz, blt, branchControl, DMwe, falling_edge, inINPUT, inputBuffer, jal,
       jr, jump, jumpControl, keyboard_1_avail, Negative, not_2_out, not_3_out, not_4_out, not_5_out,
       not_6_out, not_7_out, not_8_out, not_9_out, not_10_out, not_11_out, not_12_out, not_13_out,
       not_14_out, not_15_out, not_16_out, not_17_out, OEL, outOUTPUT, Rdst, rising_edge, Rwd, Rwe, WEL, Zero;
  wire [2:0] ALUop, RdstResult, undriven, WP;
  wire [3:0] Opcode;
  wire [6:0] inData, keyboradInput, outData;
  wire [11:0] Address;
  wire [14:0] alu_4_outputdata;
  wire [15:0] addr, afterInput, afterMem, B, branch, dataLatch, dataMem, dataOut, exImmediate1, exImmediate2,
       jumpPC, newRS2VAL, nextPC, nextTruePC, outALU, RDVAL, RS2VAL;
  wire [15:7] RS1VAL;

  Clock clk (.out(rising_edge));
  ROM #(.addrWidth(16), .dataWidth(16)) rom_1 (.addr(dataOut), .data({Opcode, Address}));
  not not_1 (falling_edge, rising_edge);
  Control control_1 (
    .opcode(Opcode), .ALUinB(ALUinB), .inINPUT(inINPUT), .outOUTPUT(outOUTPUT), .Rwd(Rwd), .DMwe(DMwe),
    .Rdst(Rdst), .jump(jump), .jal(jal), .jr(jr), .beqz(beqz), .blt(blt), .Rwe(Rwe), .ALUop(ALUop));
  oneRegister oneregister_1 (.WE(1'b1), .CLK(falling_edge), .reset(reset), .dataIn(nextTruePC), .dataOut(dataOut));
  Multiplexer #(.width(3), .enable("false")) multiplexer_1 (
    .in0(Address[8:6]), .in1(Address[5:3]), .out(RdstResult), .sel(Rdst));
  Multiplexer #(.width(3), .enable("false")) multiplexer_2 (.in0(RdstResult), .in1(3'b111), .out(WP), .sel(jal));
  ALU alu_1 (.OpType(3'b000), .InputData1(nextPC), .InputData2(exImmediate2), .OutputData(B));  // open: shamt
  extender extender_1 (.Immediate(Address[5:0]), .extendedImmediate(exImmediate2));
  ALU alu_2 (.OpType(3'b000), .InputData1(dataOut), .InputData2(16'h1), .OutputData(nextPC));  // open: shamt
  Multiplexer #(.width(16), .enable("false")) multiplexer_3 (.in0(afterInput), .in1(nextPC), .out(RDVAL), .sel(jal));
  extender extender_2 (.Immediate(Address[5:0]), .extendedImmediate(exImmediate1));
  Multiplexer #(.width(16), .enable("false")) multiplexer_4 (
    .in0(RS2VAL), .in1(exImmediate1), .out(newRS2VAL), .sel(ALUinB));
  RegisterFile registerfile_1 (
    .RDVAL(RDVAL), .reset(reset), .clk(rising_edge), .ReadReg1(Address[11:9]), .ReadReg2(Address[8:6]),
    .WE(Rwe), .WritePort(WP), .RS1VAL({RS1VAL, outData}), .RS2VAL(RS2VAL));
  RAM #(.addrWidth(16), .dataWidth(16), .trigger("high"), .databus("bibus")) ram_1 (
    .addr(addr), .we(WEL), .oe(OEL), .din(dataLatch), .dout(dataMem));
  Multiplexer #(.width(16), .enable("false")) multiplexer_5 (.in0(nextPC), .in1(B), .out(branch), .sel(branchControl));
  Multiplexer #(.width(16), .enable("false")) multiplexer_6 (
    .in0(branch), .in1({4'b0000, Address}), .out(jumpPC), .sel(jumpControl));
  Multiplexer #(.width(16), .enable("false")) multiplexer_7 (
    .in0(jumpPC), .in1({RS1VAL, outData}), .out(nextTruePC), .sel(jr));
  not not_2 (not_2_out, outData[0]);
  not not_3 (not_3_out, RS1VAL[15]);
  Multiplexer #(.width(16), .enable("false")) multiplexer_8 (
    .in0(afterMem), .in1({{8{1'b0}}, inputBuffer, keyboradInput}), .out(afterInput), .sel(inINPUT));
  not not_4 (not_4_out, outData[1]);
  not not_5 (not_5_out, outData[2]);
  not not_6 (not_6_out, outData[3]);
  not not_7 (not_7_out, RS1VAL[12]);
  not not_8 (not_8_out, RS1VAL[13]);
  not not_9 (not_9_out, RS1VAL[14]);
  and and_1 (and_1_out, beqz, Zero);
  not not_10 (not_10_out, outData[4]);
  not not_11 (not_11_out, outData[5]);
  not not_12 (not_12_out, RS1VAL[10]);
  not not_13 (not_13_out, RS1VAL[11]);
  or or_1 (branchControl, and_1_out, and_2_out);
  not not_14 (not_14_out, outData[6]);
  not not_15 (not_15_out, RS1VAL[7]);
  not not_16 (not_16_out, RS1VAL[8]);
  not not_17 (not_17_out, RS1VAL[9]);
  and and_2 (and_2_out, blt, Negative);
  ALU alu_3 (
    .OpType(ALUop), .InputData1({RS1VAL, outData}), .InputData2(newRS2VAL), .shamt(Address[2:0]),
    .OutputData(outALU));
  memory_latch memory_latch_1 (
    .address(outALU), .WE(DMwe), .clk(falling_edge), .data_in(RS2VAL), .address_latched(addr),
    .WE_latched(WEL), .OE_latched(OEL), .data_in_latched(dataLatch));
  or or_2 (jumpControl, jump, jal);
  and and_3 (Zero, not_2_out, not_4_out, not_5_out, not_6_out, not_10_out, not_11_out, not_14_out, not_15_out, not_16_out, not_17_out, not_12_out, not_13_out, not_7_out, not_8_out, not_9_out, not_3_out);
  Multiplexer #(.width(16), .enable("false")) multiplexer_9 (.in0(outALU), .in1(dataMem), .out(afterMem), .sel(Rwd));
  TTY #(.rows(13), .cols(80)) tty_1 (.data(outData), .clk(rising_edge), .we(outOUTPUT), .clr(reset));
  Keyboard keyboard_1 (.clk(falling_edge), .re(inINPUT), .clr(reset), .avail(keyboard_1_avail), .data(inData));
  Multiplexer #(.width(7), .enable("false")) multiplexer_10 (
    .in0(inData), .in1({7{1'b0}}), .out(keyboradInput), .sel(inputBuffer));
  not not_18 (inputBuffer, keyboard_1_avail);
  ALU alu_4 (
    .OpType(3'b001), .InputData1({RS1VAL, outData}), .InputData2(RS2VAL), .shamt(undriven),
    .OutputData({Negative, alu_4_outputdata}));

  // Other names for the same wires on the sheet: keyboradInput[7] = inputBuffer; bits[11:0] = Address;
  //   Immediate[5:0] = Address[5:0]; L[11:0] = Address; ROMbits[15:0] = {Opcode, Address}; Shamt[2:0] = Address[2:0];
  //   Rd[2:0] = Address[5:3]; Rt[2:0] = Address[8:6]; Rs[2:0] = Address[11:9]; RS1VAL[6:0] = outData
endmodule

module oneBitAdder (
  input  Cin,
  input  a,
  input  b,
  output sum,
  output Cout
);

  wire and_1_out, and_2_out, xor_1_out;

  xor xor_1 (xor_1_out, a, b);
  xor xor_2 (sum, xor_1_out, Cin);
  and and_1 (and_1_out, Cin, xor_1_out);
  and and_2 (and_2_out, b, a);
  or or_1 (Cout, and_1_out, and_2_out);
endmodule

module adderAndSubtracter (
  input  [15:0] A,
  input  [15:0] B,
  input  sub,
  output [15:0] result,
  output ovf
);

  wire onebitadder_1_cout, onebitadder_2_cout, onebitadder_3_cout, onebitadder_4_cout, onebitadder_5_cout,
       onebitadder_6_cout, onebitadder_7_cout, onebitadder_8_cout, onebitadder_9_cout, onebitadder_10_cout,
       onebitadder_11_cout, onebitadder_12_cout, onebitadder_13_cout, onebitadder_14_cout,
       onebitadder_15_cout, onebitadder_16_cout, xor_1_out, xor_2_out, xor_3_out, xor_4_out, xor_5_out,
       xor_6_out, xor_7_out, xor_8_out, xor_9_out, xor_10_out, xor_11_out, xor_12_out, xor_13_out,
       xor_14_out, xor_15_out, xor_16_out;

  xor xor_1 (xor_1_out, B[0], sub);
  xor xor_2 (xor_2_out, B[1], sub);
  xor xor_3 (xor_3_out, B[2], sub);
  xor xor_4 (xor_4_out, B[3], sub);
  xor xor_5 (xor_5_out, B[4], sub);
  xor xor_6 (xor_6_out, B[5], sub);
  xor xor_7 (xor_7_out, B[6], sub);
  xor xor_8 (xor_8_out, B[7], sub);
  xor xor_9 (xor_9_out, B[8], sub);
  xor xor_10 (xor_10_out, B[9], sub);
  xor xor_11 (xor_11_out, B[10], sub);
  xor xor_12 (xor_12_out, B[11], sub);
  xor xor_13 (xor_13_out, B[12], sub);
  xor xor_14 (xor_14_out, B[13], sub);
  xor xor_15 (xor_15_out, B[14], sub);
  xor xor_16 (xor_16_out, B[15], sub);
  oneBitAdder onebitadder_1 (.Cin(sub), .a(A[0]), .b(xor_1_out), .sum(result[0]), .Cout(onebitadder_1_cout));
  oneBitAdder onebitadder_2 (
    .Cin(onebitadder_1_cout), .a(A[1]), .b(xor_2_out), .sum(result[1]), .Cout(onebitadder_2_cout));
  oneBitAdder onebitadder_3 (
    .Cin(onebitadder_2_cout), .a(A[2]), .b(xor_3_out), .sum(result[2]), .Cout(onebitadder_3_cout));
  oneBitAdder onebitadder_4 (
    .Cin(onebitadder_3_cout), .a(A[3]), .b(xor_4_out), .sum(result[3]), .Cout(onebitadder_4_cout));
  oneBitAdder onebitadder_5 (
    .Cin(onebitadder_4_cout), .a(A[4]), .b(xor_5_out), .sum(result[4]), .Cout(onebitadder_5_cout));
  oneBitAdder onebitadder_6 (
    .Cin(onebitadder_5_cout), .a(A[5]), .b(xor_6_out), .sum(result[5]), .Cout(onebitadder_6_cout));
  oneBitAdder onebitadder_7 (
    .Cin(onebitadder_6_cout), .a(A[6]), .b(xor_7_out), .sum(result[6]), .Cout(onebitadder_7_cout));
  oneBitAdder onebitadder_8 (
    .Cin(onebitadder_7_cout), .a(A[7]), .b(xor_8_out), .sum(result[7]), .Cout(onebitadder_8_cout));
  oneBitAdder onebitadder_9 (
    .Cin(onebitadder_8_cout), .a(A[8]), .b(xor_9_out), .sum(result[8]), .Cout(onebitadder_9_cout));
  oneBitAdder onebitadder_10 (
    .Cin(onebitadder_9_cout), .a(A[9]), .b(xor_10_out), .sum(result[9]), .Cout(onebitadder_10_cout));
  oneBitAdder onebitadder_11 (
    .Cin(onebitadder_10_cout), .a(A[10]), .b(xor_11_out), .sum(result[10]), .Cout(onebitadder_11_cout));
  oneBitAdder onebitadder_12 (
    .Cin(onebitadder_11_cout), .a(A[11]), .b(xor_12_out), .sum(result[11]), .Cout(onebitadder_12_cout));
  oneBitAdder onebitadder_13 (
    .Cin(onebitadder_12_cout), .a(A[12]), .b(xor_13_out), .sum(result[12]), .Cout(onebitadder_13_cout));
  oneBitAdder onebitadder_14 (
    .Cin(onebitadder_13_cout), .a(A[13]), .b(xor_14_out), .sum(result[13]), .Cout(onebitadder_14_cout));
  oneBitAdder onebitadder_15 (
    .Cin(onebitadder_14_cout), .a(A[14]), .b(xor_15_out), .sum(result[14]), .Cout(onebitadder_15_cout));
  oneBitAdder onebitadder_16 (
    .Cin(onebitadder_15_cout), .a(A[15]), .b(xor_16_out), .sum(result[15]), .Cout(onebitadder_16_cout));
  xor xor_17 (ovf, onebitadder_15_cout, onebitadder_16_cout);
endmodule

module ALU (
  input  [2:0] OpType,
  input  [15:0] InputData1,
  input  [15:0] InputData2,
  input  [2:0] shamt,
  output [15:0] OutputData
);

  wire [15:0] adding, leftShifter, notOperation, rightShifter, subtracting, xorOperation;

  assign notOperation = ~InputData1;  // NOT_Gate not_1, 16 bits wide
  assign xorOperation = InputData1 ^ InputData2;  // XOR_Gate xor_1, 16 bits wide
  shiftLeft shiftleft_1 (.DataIn(InputData1), .shamt(shamt), .DataOut(leftShifter));
  shiftRight shiftright_1 (.DataIn(InputData1), .shamt(shamt), .DataOut(rightShifter));
  adderAndSubtracter adderandsubtracter_1 (.A(InputData1), .B(InputData2), .sub(1'b0), .result(adding));  // open: ovf
  adderAndSubtracter adderandsubtracter_2 (
    .A(InputData1), .B(InputData2), .sub(1'b1), .result(subtracting));  // open: ovf
  Multiplexer #(.select(3), .width(16), .enable("false")) multiplexer_1 (
    .in0(adding), .in1(subtracting), .in2(xorOperation), .in3(notOperation), .in4(leftShifter),
    .in5(rightShifter), .out(OutputData), .sel(OpType));  // open: in6, in7

  // Other names for the same wires on the sheet: In1[15:0] = InputData1; In2[15:0] = InputData2
endmodule

module Control (
  input  [3:0] opcode,
  output ALUinB,
  output inINPUT,
  output outOUTPUT,
  output Rwd,
  output DMwe,
  output Rdst,
  output jump,
  output jal,
  output jr,
  output beqz,
  output blt,
  output Rwe,
  output [2:0] ALUop
);

  wire add, addi, notInstruction, sllInstruction, srlInstruction, sub, xorInstruction;

  or or_1 (ALUinB, addi, Rwd, DMwe);
  or or_2 (ALUop[2], sllInstruction, srlInstruction);
  Decoder #(.select(4), .enable("false")) decoder_1 (
    .out0(add), .out1(sub), .out2(addi), .out3(notInstruction), .out4(xorInstruction), .out5(sllInstruction),
    .out6(srlInstruction), .out7(Rwd), .out8(DMwe), .out9(beqz), .out10(blt), .out11(jump), .out12(jr),
    .out13(jal), .out14(inINPUT), .out15(outOUTPUT), .sel(opcode));
  or or_3 (ALUop[1], xorInstruction, notInstruction);
  or or_4 (ALUop[0], sub, notInstruction, srlInstruction);
  or or_5 (Rdst, add, sub, notInstruction, xorInstruction, sllInstruction, srlInstruction, inINPUT);
  or or_6 (Rwe, add, sub, addi, notInstruction, xorInstruction, sllInstruction, srlInstruction, Rwd, jal, inINPUT);

  // Other names for the same wires on the sheet: inputInstruction = inINPUT; j = jump; lw = Rwd;
  //   outputInstruction = outOUTPUT; sw = DMwe
endmodule

module memory_latch (
  input  [15:0] address,
  input  WE,
  input  clk,
  input  [15:0] data_in,
  output [15:0] address_latched,
  output WE_latched,
  output OE_latched,
  output [15:0] data_in_latched
);

  wire DMwe_latch_q;
  wire [15:0] addr_latch_q;

  Register #(.width(16), .trigger("falling")) addr_latch (
    .D(address), .en(WE), .clk(clk), .Q(addr_latch_q));  // open: clr
  D_Flip_Flop #(.trigger("falling")) DMwe_latch (.D(WE), .clk(clk), .Q(DMwe_latch_q));  // open: Qn, preset, reset
  Register #(.width(16), .trigger("falling")) data_to_be_written (
    .D(data_in), .en(WE), .clk(clk), .Q(data_in_latched));  // open: clr
  Multiplexer #(.width(16), .enable("false")) multiplexer_1 (
    .in0(address), .in1(addr_latch_q), .out(address_latched), .sel(DMwe_latch_q));
  and and_1 (WE_latched, clk, DMwe_latch_q);
  not not_1 (OE_latched, WE_latched);
endmodule

module oneRegister (
  input  WE,
  input  CLK,
  input  reset,
  input  [15:0] dataIn,
  output [15:0] dataOut
);

  wire clk_t;

  D_Flip_Flop d_ff_1 (.D(dataIn[0]), .clk(clk_t), .Q(dataOut[0]), .reset(reset));  // open: Qn, preset
  D_Flip_Flop d_ff_2 (.D(dataIn[1]), .clk(clk_t), .Q(dataOut[1]), .reset(reset));  // open: Qn, preset
  D_Flip_Flop d_ff_3 (.D(dataIn[2]), .clk(clk_t), .Q(dataOut[2]), .reset(reset));  // open: Qn, preset
  D_Flip_Flop d_ff_4 (.D(dataIn[3]), .clk(clk_t), .Q(dataOut[3]), .reset(reset));  // open: Qn, preset
  and and_1 (clk_t, WE, CLK);
  D_Flip_Flop d_ff_5 (.D(dataIn[4]), .clk(clk_t), .Q(dataOut[4]), .reset(reset));  // open: Qn, preset
  D_Flip_Flop d_ff_6 (.D(dataIn[5]), .clk(clk_t), .Q(dataOut[5]), .reset(reset));  // open: Qn, preset
  D_Flip_Flop d_ff_7 (.D(dataIn[6]), .clk(clk_t), .Q(dataOut[6]), .reset(reset));  // open: Qn, preset
  D_Flip_Flop d_ff_8 (.D(dataIn[7]), .clk(clk_t), .Q(dataOut[7]), .reset(reset));  // open: Qn, preset
  D_Flip_Flop d_ff_9 (.D(dataIn[8]), .clk(clk_t), .Q(dataOut[8]), .reset(reset));  // open: Qn, preset
  D_Flip_Flop d_ff_10 (.D(dataIn[9]), .clk(clk_t), .Q(dataOut[9]), .reset(reset));  // open: Qn, preset
  D_Flip_Flop d_ff_11 (.D(dataIn[10]), .clk(clk_t), .Q(dataOut[10]), .reset(reset));  // open: Qn, preset
  D_Flip_Flop d_ff_12 (.D(dataIn[11]), .clk(clk_t), .Q(dataOut[11]), .reset(reset));  // open: Qn, preset
  D_Flip_Flop d_ff_13 (.D(dataIn[12]), .clk(clk_t), .Q(dataOut[12]), .reset(reset));  // open: Qn, preset
  D_Flip_Flop d_ff_14 (.D(dataIn[13]), .clk(clk_t), .Q(dataOut[13]), .reset(reset));  // open: Qn, preset
  D_Flip_Flop d_ff_15 (.D(dataIn[14]), .clk(clk_t), .Q(dataOut[14]), .reset(reset));  // open: Qn, preset
  D_Flip_Flop d_ff_16 (.D(dataIn[15]), .clk(clk_t), .Q(dataOut[15]), .reset(reset));  // open: Qn, preset

  // Other names for the same wires on the sheet: In0 = dataIn[0]; In1 = dataIn[1]; In2 = dataIn[2]; In3 = dataIn[3];
  //   In4 = dataIn[4]; In5 = dataIn[5]; In6 = dataIn[6]; In7 = dataIn[7]; In8 = dataIn[8]; In9 = dataIn[9];
  //   In10 = dataIn[10]; In11 = dataIn[11]; In12 = dataIn[12]; In13 = dataIn[13]; In14 = dataIn[14];
  //   In15 = dataIn[15]; Out0 = dataOut[0]; Out1 = dataOut[1]; Out2 = dataOut[2]; Out3 = dataOut[3];
  //   Out4 = dataOut[4]; Out5 = dataOut[5]; Out6 = dataOut[6]; Out7 = dataOut[7]; Out8 = dataOut[8];
  //   Out9 = dataOut[9]; Out10 = dataOut[10]; Out11 = dataOut[11]; Out12 = dataOut[12]; Out13 = dataOut[13];
  //   Out14 = dataOut[14]; Out15 = dataOut[15]
endmodule

module shiftLeft (
  input  [15:0] DataIn,
  input  [2:0] shamt,
  output [15:0] DataOut
);

  wire multiplexer_1_out, multiplexer_2_out, multiplexer_3_out, multiplexer_4_out, multiplexer_5_out,
       multiplexer_6_out, multiplexer_7_out, multiplexer_8_out, multiplexer_9_out, multiplexer_10_out,
       multiplexer_11_out, multiplexer_12_out, multiplexer_13_out, multiplexer_14_out, multiplexer_15_out,
       multiplexer_16_out, multiplexer_17_out, multiplexer_18_out, multiplexer_19_out, multiplexer_20_out,
       multiplexer_21_out, multiplexer_22_out, multiplexer_23_out, multiplexer_24_out, multiplexer_25_out,
       multiplexer_26_out, multiplexer_27_out, multiplexer_28_out, multiplexer_29_out, multiplexer_30_out,
       multiplexer_31_out, multiplexer_32_out;

  Multiplexer #(.enable("false")) multiplexer_1 (.in0(DataIn[0]), .in1(1'b0), .out(multiplexer_1_out), .sel(shamt[0]));
  Multiplexer #(.enable("false")) multiplexer_2 (
    .in0(DataIn[1]), .in1(DataIn[0]), .out(multiplexer_2_out), .sel(shamt[0]));
  Multiplexer #(.enable("false")) multiplexer_3 (
    .in0(DataIn[2]), .in1(DataIn[1]), .out(multiplexer_3_out), .sel(shamt[0]));
  Multiplexer #(.enable("false")) multiplexer_4 (
    .in0(DataIn[3]), .in1(DataIn[2]), .out(multiplexer_4_out), .sel(shamt[0]));
  Multiplexer #(.enable("false")) multiplexer_5 (
    .in0(DataIn[4]), .in1(DataIn[3]), .out(multiplexer_5_out), .sel(shamt[0]));
  Multiplexer #(.enable("false")) multiplexer_6 (
    .in0(DataIn[5]), .in1(DataIn[4]), .out(multiplexer_6_out), .sel(shamt[0]));
  Multiplexer #(.enable("false")) multiplexer_7 (
    .in0(DataIn[6]), .in1(DataIn[5]), .out(multiplexer_7_out), .sel(shamt[0]));
  Multiplexer #(.enable("false")) multiplexer_8 (
    .in0(DataIn[7]), .in1(DataIn[6]), .out(multiplexer_8_out), .sel(shamt[0]));
  Multiplexer #(.enable("false")) multiplexer_9 (
    .in0(DataIn[8]), .in1(DataIn[7]), .out(multiplexer_9_out), .sel(shamt[0]));
  Multiplexer #(.enable("false")) multiplexer_10 (
    .in0(DataIn[9]), .in1(DataIn[8]), .out(multiplexer_10_out), .sel(shamt[0]));
  Multiplexer #(.enable("false")) multiplexer_11 (
    .in0(DataIn[10]), .in1(DataIn[9]), .out(multiplexer_11_out), .sel(shamt[0]));
  Multiplexer #(.enable("false")) multiplexer_12 (
    .in0(DataIn[11]), .in1(DataIn[10]), .out(multiplexer_12_out), .sel(shamt[0]));
  Multiplexer #(.enable("false")) multiplexer_13 (
    .in0(DataIn[12]), .in1(DataIn[11]), .out(multiplexer_13_out), .sel(shamt[0]));
  Multiplexer #(.enable("false")) multiplexer_14 (
    .in0(DataIn[13]), .in1(DataIn[12]), .out(multiplexer_14_out), .sel(shamt[0]));
  Multiplexer #(.enable("false")) multiplexer_15 (
    .in0(DataIn[14]), .in1(DataIn[13]), .out(multiplexer_15_out), .sel(shamt[0]));
  Multiplexer #(.enable("false")) multiplexer_16 (
    .in0(DataIn[15]), .in1(DataIn[14]), .out(multiplexer_16_out), .sel(shamt[0]));
  Multiplexer #(.enable("false")) multiplexer_17 (
    .in0(multiplexer_1_out), .in1(1'b0), .out(multiplexer_17_out), .sel(shamt[1]));
  Multiplexer #(.enable("false")) multiplexer_18 (
    .in0(multiplexer_2_out), .in1(1'b0), .out(multiplexer_18_out), .sel(shamt[1]));
  Multiplexer #(.enable("false")) multiplexer_19 (
    .in0(multiplexer_3_out), .in1(multiplexer_1_out), .out(multiplexer_19_out), .sel(shamt[1]));
  Multiplexer #(.enable("false")) multiplexer_20 (
    .in0(multiplexer_4_out), .in1(multiplexer_2_out), .out(multiplexer_20_out), .sel(shamt[1]));
  Multiplexer #(.enable("false")) multiplexer_21 (
    .in0(multiplexer_5_out), .in1(multiplexer_3_out), .out(multiplexer_21_out), .sel(shamt[1]));
  Multiplexer #(.enable("false")) multiplexer_22 (
    .in0(multiplexer_6_out), .in1(multiplexer_4_out), .out(multiplexer_22_out), .sel(shamt[1]));
  Multiplexer #(.enable("false")) multiplexer_23 (
    .in0(multiplexer_7_out), .in1(multiplexer_5_out), .out(multiplexer_23_out), .sel(shamt[1]));
  Multiplexer #(.enable("false")) multiplexer_24 (
    .in0(multiplexer_8_out), .in1(multiplexer_6_out), .out(multiplexer_24_out), .sel(shamt[1]));
  Multiplexer #(.enable("false")) multiplexer_25 (
    .in0(multiplexer_9_out), .in1(multiplexer_7_out), .out(multiplexer_25_out), .sel(shamt[1]));
  Multiplexer #(.enable("false")) multiplexer_26 (
    .in0(multiplexer_10_out), .in1(multiplexer_8_out), .out(multiplexer_26_out), .sel(shamt[1]));
  Multiplexer #(.enable("false")) multiplexer_27 (
    .in0(multiplexer_11_out), .in1(multiplexer_9_out), .out(multiplexer_27_out), .sel(shamt[1]));
  Multiplexer #(.enable("false")) multiplexer_28 (
    .in0(multiplexer_12_out), .in1(multiplexer_10_out), .out(multiplexer_28_out), .sel(shamt[1]));
  Multiplexer #(.enable("false")) multiplexer_29 (
    .in0(multiplexer_13_out), .in1(multiplexer_11_out), .out(multiplexer_29_out), .sel(shamt[1]));
  Multiplexer #(.enable("false")) multiplexer_30 (
    .in0(multiplexer_14_out), .in1(multiplexer_12_out), .out(multiplexer_30_out), .sel(shamt[1]));
  Multiplexer #(.enable("false")) multiplexer_31 (
    .in0(multiplexer_15_out), .in1(multiplexer_13_out), .out(multiplexer_31_out), .sel(shamt[1]));
  Multiplexer #(.enable("false")) multiplexer_32 (
    .in0(multiplexer_16_out), .in1(multiplexer_14_out), .out(multiplexer_32_out), .sel(shamt[1]));
  Multiplexer #(.enable("false")) multiplexer_33 (
    .in0(multiplexer_17_out), .in1(1'b0), .out(DataOut[0]), .sel(shamt[2]));
  Multiplexer #(.enable("false")) multiplexer_34 (
    .in0(multiplexer_18_out), .in1(1'b0), .out(DataOut[1]), .sel(shamt[2]));
  Multiplexer #(.enable("false")) multiplexer_35 (
    .in0(multiplexer_19_out), .in1(1'b0), .out(DataOut[2]), .sel(shamt[2]));
  Multiplexer #(.enable("false")) multiplexer_36 (
    .in0(multiplexer_20_out), .in1(1'b0), .out(DataOut[3]), .sel(shamt[2]));
  Multiplexer #(.enable("false")) multiplexer_37 (
    .in0(multiplexer_21_out), .in1(multiplexer_17_out), .out(DataOut[4]), .sel(shamt[2]));
  Multiplexer #(.enable("false")) multiplexer_38 (
    .in0(multiplexer_22_out), .in1(multiplexer_18_out), .out(DataOut[5]), .sel(shamt[2]));
  Multiplexer #(.enable("false")) multiplexer_39 (
    .in0(multiplexer_23_out), .in1(multiplexer_19_out), .out(DataOut[6]), .sel(shamt[2]));
  Multiplexer #(.enable("false")) multiplexer_40 (
    .in0(multiplexer_24_out), .in1(multiplexer_20_out), .out(DataOut[7]), .sel(shamt[2]));
  Multiplexer #(.enable("false")) multiplexer_41 (
    .in0(multiplexer_25_out), .in1(multiplexer_21_out), .out(DataOut[8]), .sel(shamt[2]));
  Multiplexer #(.enable("false")) multiplexer_42 (
    .in0(multiplexer_26_out), .in1(multiplexer_22_out), .out(DataOut[9]), .sel(shamt[2]));
  Multiplexer #(.enable("false")) multiplexer_43 (
    .in0(multiplexer_27_out), .in1(multiplexer_23_out), .out(DataOut[10]), .sel(shamt[2]));
  Multiplexer #(.enable("false")) multiplexer_44 (
    .in0(multiplexer_28_out), .in1(multiplexer_24_out), .out(DataOut[11]), .sel(shamt[2]));
  Multiplexer #(.enable("false")) multiplexer_45 (
    .in0(multiplexer_29_out), .in1(multiplexer_25_out), .out(DataOut[12]), .sel(shamt[2]));
  Multiplexer #(.enable("false")) multiplexer_46 (
    .in0(multiplexer_30_out), .in1(multiplexer_26_out), .out(DataOut[13]), .sel(shamt[2]));
  Multiplexer #(.enable("false")) multiplexer_47 (
    .in0(multiplexer_31_out), .in1(multiplexer_27_out), .out(DataOut[14]), .sel(shamt[2]));
  Multiplexer #(.enable("false")) multiplexer_48 (
    .in0(multiplexer_32_out), .in1(multiplexer_28_out), .out(DataOut[15]), .sel(shamt[2]));

  // Other names for the same wires on the sheet: In0 = DataIn[0]; In1 = DataIn[1]; In2 = DataIn[2]; In3 = DataIn[3];
  //   In4 = DataIn[4]; In5 = DataIn[5]; In6 = DataIn[6]; In7 = DataIn[7]; In8 = DataIn[8]; In9 = DataIn[9];
  //   In10 = DataIn[10]; In11 = DataIn[11]; In12 = DataIn[12]; In13 = DataIn[13]; In14 = DataIn[14];
  //   In15 = DataIn[15]; Out0 = DataOut[0]; Out1 = DataOut[1]; Out2 = DataOut[2]; Out3 = DataOut[3];
  //   Out4 = DataOut[4]; Out5 = DataOut[5]; Out6 = DataOut[6]; Out7 = DataOut[7]; Out8 = DataOut[8];
  //   Out9 = DataOut[9]; Out10 = DataOut[10]; Out11 = DataOut[11]; Out12 = DataOut[12]; Out13 = DataOut[13];
  //   Out14 = DataOut[14]; Out15 = DataOut[15]; bit0 = shamt[0]; bit1 = shamt[1]; bit2 = shamt[2]
endmodule

module shiftRight (
  input  [15:0] DataIn,
  input  [2:0] shamt,
  output [15:0] DataOut
);

  wire multiplexer_1_out, multiplexer_2_out, multiplexer_3_out, multiplexer_4_out, multiplexer_5_out,
       multiplexer_6_out, multiplexer_7_out, multiplexer_8_out, multiplexer_9_out, multiplexer_10_out,
       multiplexer_11_out, multiplexer_12_out, multiplexer_13_out, multiplexer_14_out, multiplexer_15_out,
       multiplexer_16_out, multiplexer_17_out, multiplexer_18_out, multiplexer_19_out, multiplexer_20_out,
       multiplexer_21_out, multiplexer_22_out, multiplexer_23_out, multiplexer_24_out, multiplexer_25_out,
       multiplexer_26_out, multiplexer_27_out, multiplexer_28_out, multiplexer_29_out, multiplexer_30_out,
       multiplexer_31_out, multiplexer_32_out;

  Multiplexer #(.enable("false")) multiplexer_1 (.in0(DataIn[15]), .in1(1'b0), .out(multiplexer_1_out), .sel(shamt[0]));
  Multiplexer #(.enable("false")) multiplexer_2 (
    .in0(DataIn[14]), .in1(DataIn[15]), .out(multiplexer_2_out), .sel(shamt[0]));
  Multiplexer #(.enable("false")) multiplexer_3 (
    .in0(DataIn[13]), .in1(DataIn[14]), .out(multiplexer_3_out), .sel(shamt[0]));
  Multiplexer #(.enable("false")) multiplexer_4 (
    .in0(DataIn[12]), .in1(DataIn[13]), .out(multiplexer_4_out), .sel(shamt[0]));
  Multiplexer #(.enable("false")) multiplexer_5 (
    .in0(DataIn[11]), .in1(DataIn[12]), .out(multiplexer_5_out), .sel(shamt[0]));
  Multiplexer #(.enable("false")) multiplexer_6 (
    .in0(DataIn[10]), .in1(DataIn[11]), .out(multiplexer_6_out), .sel(shamt[0]));
  Multiplexer #(.enable("false")) multiplexer_7 (
    .in0(DataIn[9]), .in1(DataIn[10]), .out(multiplexer_7_out), .sel(shamt[0]));
  Multiplexer #(.enable("false")) multiplexer_8 (
    .in0(DataIn[8]), .in1(DataIn[9]), .out(multiplexer_8_out), .sel(shamt[0]));
  Multiplexer #(.enable("false")) multiplexer_9 (
    .in0(DataIn[7]), .in1(DataIn[8]), .out(multiplexer_9_out), .sel(shamt[0]));
  Multiplexer #(.enable("false")) multiplexer_10 (
    .in0(DataIn[6]), .in1(DataIn[7]), .out(multiplexer_10_out), .sel(shamt[0]));
  Multiplexer #(.enable("false")) multiplexer_11 (
    .in0(DataIn[5]), .in1(DataIn[6]), .out(multiplexer_11_out), .sel(shamt[0]));
  Multiplexer #(.enable("false")) multiplexer_12 (
    .in0(DataIn[4]), .in1(DataIn[5]), .out(multiplexer_12_out), .sel(shamt[0]));
  Multiplexer #(.enable("false")) multiplexer_13 (
    .in0(DataIn[3]), .in1(DataIn[4]), .out(multiplexer_13_out), .sel(shamt[0]));
  Multiplexer #(.enable("false")) multiplexer_14 (
    .in0(DataIn[2]), .in1(DataIn[3]), .out(multiplexer_14_out), .sel(shamt[0]));
  Multiplexer #(.enable("false")) multiplexer_15 (
    .in0(DataIn[1]), .in1(DataIn[2]), .out(multiplexer_15_out), .sel(shamt[0]));
  Multiplexer #(.enable("false")) multiplexer_16 (
    .in0(DataIn[0]), .in1(DataIn[1]), .out(multiplexer_16_out), .sel(shamt[0]));
  Multiplexer #(.enable("false")) multiplexer_17 (
    .in0(multiplexer_1_out), .in1(1'b0), .out(multiplexer_17_out), .sel(shamt[1]));
  Multiplexer #(.enable("false")) multiplexer_18 (
    .in0(multiplexer_2_out), .in1(1'b0), .out(multiplexer_18_out), .sel(shamt[1]));
  Multiplexer #(.enable("false")) multiplexer_19 (
    .in0(multiplexer_3_out), .in1(multiplexer_1_out), .out(multiplexer_19_out), .sel(shamt[1]));
  Multiplexer #(.enable("false")) multiplexer_20 (
    .in0(multiplexer_4_out), .in1(multiplexer_2_out), .out(multiplexer_20_out), .sel(shamt[1]));
  Multiplexer #(.enable("false")) multiplexer_21 (
    .in0(multiplexer_5_out), .in1(multiplexer_3_out), .out(multiplexer_21_out), .sel(shamt[1]));
  Multiplexer #(.enable("false")) multiplexer_22 (
    .in0(multiplexer_6_out), .in1(multiplexer_4_out), .out(multiplexer_22_out), .sel(shamt[1]));
  Multiplexer #(.enable("false")) multiplexer_23 (
    .in0(multiplexer_7_out), .in1(multiplexer_5_out), .out(multiplexer_23_out), .sel(shamt[1]));
  Multiplexer #(.enable("false")) multiplexer_24 (
    .in0(multiplexer_8_out), .in1(multiplexer_6_out), .out(multiplexer_24_out), .sel(shamt[1]));
  Multiplexer #(.enable("false")) multiplexer_25 (
    .in0(multiplexer_9_out), .in1(multiplexer_7_out), .out(multiplexer_25_out), .sel(shamt[1]));
  Multiplexer #(.enable("false")) multiplexer_26 (
    .in0(multiplexer_10_out), .in1(multiplexer_8_out), .out(multiplexer_26_out), .sel(shamt[1]));
  Multiplexer #(.enable("false")) multiplexer_27 (
    .in0(multiplexer_11_out), .in1(multiplexer_9_out), .out(multiplexer_27_out), .sel(shamt[1]));
  Multiplexer #(.enable("false")) multiplexer_28 (
    .in0(multiplexer_12_out), .in1(multiplexer_10_out), .out(multiplexer_28_out), .sel(shamt[1]));
  Multiplexer #(.enable("false")) multiplexer_29 (
    .in0(multiplexer_13_out), .in1(multiplexer_11_out), .out(multiplexer_29_out), .sel(shamt[1]));
  Multiplexer #(.enable("false")) multiplexer_30 (
    .in0(multiplexer_14_out), .in1(multiplexer_12_out), .out(multiplexer_30_out), .sel(shamt[1]));
  Multiplexer #(.enable("false")) multiplexer_31 (
    .in0(multiplexer_15_out), .in1(multiplexer_13_out), .out(multiplexer_31_out), .sel(shamt[1]));
  Multiplexer #(.enable("false")) multiplexer_32 (
    .in0(multiplexer_16_out), .in1(multiplexer_14_out), .out(multiplexer_32_out), .sel(shamt[1]));
  Multiplexer #(.enable("false")) multiplexer_33 (
    .in0(multiplexer_17_out), .in1(1'b0), .out(DataOut[15]), .sel(shamt[2]));
  Multiplexer #(.enable("false")) multiplexer_34 (
    .in0(multiplexer_18_out), .in1(1'b0), .out(DataOut[14]), .sel(shamt[2]));
  Multiplexer #(.enable("false")) multiplexer_35 (
    .in0(multiplexer_19_out), .in1(1'b0), .out(DataOut[13]), .sel(shamt[2]));
  Multiplexer #(.enable("false")) multiplexer_36 (
    .in0(multiplexer_20_out), .in1(1'b0), .out(DataOut[12]), .sel(shamt[2]));
  Multiplexer #(.enable("false")) multiplexer_37 (
    .in0(multiplexer_21_out), .in1(multiplexer_17_out), .out(DataOut[11]), .sel(shamt[2]));
  Multiplexer #(.enable("false")) multiplexer_38 (
    .in0(multiplexer_22_out), .in1(multiplexer_18_out), .out(DataOut[10]), .sel(shamt[2]));
  Multiplexer #(.enable("false")) multiplexer_39 (
    .in0(multiplexer_23_out), .in1(multiplexer_19_out), .out(DataOut[9]), .sel(shamt[2]));
  Multiplexer #(.enable("false")) multiplexer_40 (
    .in0(multiplexer_24_out), .in1(multiplexer_20_out), .out(DataOut[8]), .sel(shamt[2]));
  Multiplexer #(.enable("false")) multiplexer_41 (
    .in0(multiplexer_25_out), .in1(multiplexer_21_out), .out(DataOut[7]), .sel(shamt[2]));
  Multiplexer #(.enable("false")) multiplexer_42 (
    .in0(multiplexer_26_out), .in1(multiplexer_22_out), .out(DataOut[6]), .sel(shamt[2]));
  Multiplexer #(.enable("false")) multiplexer_43 (
    .in0(multiplexer_27_out), .in1(multiplexer_23_out), .out(DataOut[5]), .sel(shamt[2]));
  Multiplexer #(.enable("false")) multiplexer_44 (
    .in0(multiplexer_28_out), .in1(multiplexer_24_out), .out(DataOut[4]), .sel(shamt[2]));
  Multiplexer #(.enable("false")) multiplexer_45 (
    .in0(multiplexer_29_out), .in1(multiplexer_25_out), .out(DataOut[3]), .sel(shamt[2]));
  Multiplexer #(.enable("false")) multiplexer_46 (
    .in0(multiplexer_30_out), .in1(multiplexer_26_out), .out(DataOut[2]), .sel(shamt[2]));
  Multiplexer #(.enable("false")) multiplexer_47 (
    .in0(multiplexer_31_out), .in1(multiplexer_27_out), .out(DataOut[1]), .sel(shamt[2]));
  Multiplexer #(.enable("false")) multiplexer_48 (
    .in0(multiplexer_32_out), .in1(multiplexer_28_out), .out(DataOut[0]), .sel(shamt[2]));

  // Other names for the same wires on the sheet: In0 = DataIn[0]; In1 = DataIn[1]; In2 = DataIn[2]; In3 = DataIn[3];
  //   In4 = DataIn[4]; In5 = DataIn[5]; In6 = DataIn[6]; In7 = DataIn[7]; In8 = DataIn[8]; In9 = DataIn[9];
  //   In10 = DataIn[10]; In11 = DataIn[11]; In12 = DataIn[12]; In13 = DataIn[13]; In14 = DataIn[14];
  //   In15 = DataIn[15]; Out0 = DataOut[0]; Out1 = DataOut[1]; Out2 = DataOut[2]; Out3 = DataOut[3];
  //   Out4 = DataOut[4]; Out5 = DataOut[5]; Out6 = DataOut[6]; Out7 = DataOut[7]; Out8 = DataOut[8];
  //   Out9 = DataOut[9]; Out10 = DataOut[10]; Out11 = DataOut[11]; Out12 = DataOut[12]; Out13 = DataOut[13];
  //   Out14 = DataOut[14]; Out15 = DataOut[15]; bit0 = shamt[0]; bit1 = shamt[1]; bit2 = shamt[2]
endmodule

module RegisterFile (
  input  [15:0] RDVAL,
  input  reset,
  input  clk,
  input  [2:0] ReadReg1,
  input  [2:0] ReadReg2,
  input  WE,
  input  [2:0] WritePort,
  output [15:0] RS1VAL,
  output [15:0] RS2VAL
);

  wire out1bit0, out1bit1, out1bit2, out1bit3, out1bit4, out1bit5, out1bit6, out1bit7, out2bit0, out2bit1,
       out2bit2, out2bit3, out2bit4, out2bit5, out2bit6, out2bit7, WE1, WE2, WE3, WE4, WE5, WE6, WE7;
  wire [15:0] oneregister_1_dataout, oneregister_2_dataout, oneregister_3_dataout, oneregister_4_dataout,
       oneregister_5_dataout, oneregister_6_dataout, oneregister_7_dataout;

  Decoder #(.select(3)) decoder_1 (
    .out0(out1bit0), .out1(out1bit1), .out2(out1bit2), .out3(out1bit3), .out4(out1bit4), .out5(out1bit5),
    .out6(out1bit6), .out7(out1bit7), .sel(ReadReg1));  // open: en
  Decoder #(.select(3)) decoder_2 (
    .out0(out2bit0), .out1(out2bit1), .out2(out2bit2), .out3(out2bit3), .out4(out2bit4), .out5(out2bit5),
    .out6(out2bit6), .out7(out2bit7), .sel(ReadReg2));  // open: en
  Decoder #(.select(3)) decoder_3 (
    .out1(WE1), .out2(WE2), .out3(WE3), .out4(WE4), .out5(WE5), .out6(WE6), .out7(WE7), .sel(WritePort),
    .en(WE));  // open: out0
  // Probe on {16{1'b0}}
  // Probe on oneregister_1_dataout
  oneRegister oneregister_1 (.WE(WE1), .CLK(clk), .reset(reset), .dataIn(RDVAL), .dataOut(oneregister_1_dataout));
  // Probe on oneregister_2_dataout
  oneRegister oneregister_2 (.WE(WE2), .CLK(clk), .reset(reset), .dataIn(RDVAL), .dataOut(oneregister_2_dataout));
  // Probe on oneregister_3_dataout
  oneRegister oneregister_3 (.WE(WE3), .CLK(clk), .reset(reset), .dataIn(RDVAL), .dataOut(oneregister_3_dataout));
  // Probe on oneregister_4_dataout
  oneRegister oneregister_4 (.WE(WE4), .CLK(clk), .reset(reset), .dataIn(RDVAL), .dataOut(oneregister_4_dataout));
  // Probe on oneregister_5_dataout
  oneRegister oneregister_5 (.WE(WE5), .CLK(clk), .reset(reset), .dataIn(RDVAL), .dataOut(oneregister_5_dataout));
  // Probe on oneregister_6_dataout
  oneRegister oneregister_6 (.WE(WE6), .CLK(clk), .reset(reset), .dataIn(RDVAL), .dataOut(oneregister_6_dataout));
  // Probe on oneregister_7_dataout
  oneRegister oneregister_7 (.WE(WE7), .CLK(clk), .reset(reset), .dataIn(RDVAL), .dataOut(oneregister_7_dataout));
  assign RS1VAL = out1bit0 ? {16{1'b0}} : 16'bz;  // Controlled_Buffer controlled_buffer_1
  assign RS2VAL = out2bit0 ? {16{1'b0}} : 16'bz;  // Controlled_Buffer controlled_buffer_2
  assign RS1VAL = out1bit1 ? oneregister_1_dataout : 16'bz;  // Controlled_Buffer controlled_buffer_3
  assign RS2VAL = out2bit1 ? oneregister_1_dataout : 16'bz;  // Controlled_Buffer controlled_buffer_4
  assign RS1VAL = out1bit2 ? oneregister_2_dataout : 16'bz;  // Controlled_Buffer controlled_buffer_5
  assign RS2VAL = out2bit2 ? oneregister_2_dataout : 16'bz;  // Controlled_Buffer controlled_buffer_6
  assign RS1VAL = out1bit3 ? oneregister_3_dataout : 16'bz;  // Controlled_Buffer controlled_buffer_7
  assign RS2VAL = out2bit3 ? oneregister_3_dataout : 16'bz;  // Controlled_Buffer controlled_buffer_8
  assign RS1VAL = out1bit4 ? oneregister_4_dataout : 16'bz;  // Controlled_Buffer controlled_buffer_9
  assign RS2VAL = out2bit4 ? oneregister_4_dataout : 16'bz;  // Controlled_Buffer controlled_buffer_10
  assign RS1VAL = out1bit5 ? oneregister_5_dataout : 16'bz;  // Controlled_Buffer controlled_buffer_11
  assign RS2VAL = out2bit5 ? oneregister_5_dataout : 16'bz;  // Controlled_Buffer controlled_buffer_12
  assign RS1VAL = out1bit6 ? oneregister_6_dataout : 16'bz;  // Controlled_Buffer controlled_buffer_13
  assign RS2VAL = out2bit6 ? oneregister_6_dataout : 16'bz;  // Controlled_Buffer controlled_buffer_14
  assign RS1VAL = out1bit7 ? oneregister_7_dataout : 16'bz;  // Controlled_Buffer controlled_buffer_15
  assign RS2VAL = out2bit7 ? oneregister_7_dataout : 16'bz;  // Controlled_Buffer controlled_buffer_16
endmodule

module extender (
  input  [5:0] Immediate,
  output [15:0] extendedImmediate
);

  Multiplexer #(.enable("false")) multiplexer_1 (
    .in0(1'b0), .in1(1'b1), .out(extendedImmediate[6]), .sel(Immediate[5]));
  Multiplexer #(.enable("false")) multiplexer_2 (
    .in0(1'b0), .in1(1'b1), .out(extendedImmediate[11]), .sel(Immediate[5]));
  Multiplexer #(.enable("false")) multiplexer_3 (
    .in0(1'b0), .in1(1'b1), .out(extendedImmediate[12]), .sel(Immediate[5]));
  Multiplexer #(.enable("false")) multiplexer_4 (
    .in0(1'b0), .in1(1'b1), .out(extendedImmediate[13]), .sel(Immediate[5]));
  Multiplexer #(.enable("false")) multiplexer_5 (
    .in0(1'b0), .in1(1'b1), .out(extendedImmediate[14]), .sel(Immediate[5]));
  Multiplexer #(.enable("false")) multiplexer_6 (
    .in0(1'b0), .in1(1'b1), .out(extendedImmediate[15]), .sel(Immediate[5]));
  Multiplexer #(.enable("false")) multiplexer_7 (
    .in0(1'b0), .in1(1'b1), .out(extendedImmediate[7]), .sel(Immediate[5]));
  Multiplexer #(.enable("false")) multiplexer_8 (
    .in0(1'b0), .in1(1'b1), .out(extendedImmediate[8]), .sel(Immediate[5]));
  Multiplexer #(.enable("false")) multiplexer_9 (
    .in0(1'b0), .in1(1'b1), .out(extendedImmediate[9]), .sel(Immediate[5]));
  Multiplexer #(.enable("false")) multiplexer_10 (
    .in0(1'b0), .in1(1'b1), .out(extendedImmediate[10]), .sel(Immediate[5]));

  assign extendedImmediate[5:0] = Immediate;
endmodule
