// Logisim project my_adder.circ as structural Verilog: 2 circuits, main circuit main
module main (
  input  [15:0] A,
  input  [15:0] B,
  input  sub,
  output [15:0] result,
  output ovf
);

  wire one_bit_adder_1_cout, one_bit_adder_2_cout, one_bit_adder_3_cout, one_bit_adder_4_cout,
       one_bit_adder_5_cout, one_bit_adder_6_cout, one_bit_adder_7_cout, one_bit_adder_8_cout,
       one_bit_adder_9_cout, one_bit_adder_10_cout, one_bit_adder_11_cout, one_bit_adder_12_cout,
       one_bit_adder_13_cout, one_bit_adder_14_cout, one_bit_adder_15_cout, one_bit_adder_16_cout, xor_1_out,
       xor_2_out, xor_3_out, xor_4_out, xor_5_out, xor_6_out, xor_7_out, xor_8_out, xor_9_out, xor_10_out,
       xor_11_out, xor_12_out, xor_13_out, xor_14_out, xor_15_out, xor_16_out;

  xor xor_1 (xor_1_out, B[0], sub);
  xor xor_2 (xor_2_out, B[1], sub);
  xor xor_3 (xor_3_out, B[2], sub);
  xor xor_4 (xor_4_out, B[3], sub);
  xor xor_5 (xor_5_out, B[4], sub);
  xor xor_6 (xor_6_out, B[5], sub);
  xor xor_7 (xor_7_out, B[6], sub);
  xor xor_8 (xor_8_out, B[7], sub);
  xor xor_9 (xor_9_out, B[8], sub);
  xor xor_10 (xor_10_out, B[9], sub);
  xor xor_11 (xor_11_out, B[10], sub);
  xor xor_12 (xor_12_out, B[11], sub);
  xor xor_13 (xor_13_out, B[12], sub);
  xor xor_14 (xor_14_out, B[13], sub);
  xor xor_15 (xor_15_out, B[14], sub);
  xor xor_16 (xor_16_out, B[15], sub);
  one_bit_adder one_bit_adder_1 (.Cin(sub), .a(A[0]), .b(xor_1_out), .sum(result[0]), .Cout(one_bit_adder_1_cout));
  one_bit_adder one_bit_adder_2 (
    .Cin(one_bit_adder_1_cout), .a(A[1]), .b(xor_2_out), .sum(result[1]), .Cout(one_bit_adder_2_cout));
  one_bit_adder one_bit_adder_3 (
    .Cin(one_bit_adder_2_cout), .a(A[2]), .b(xor_3_out), .sum(result[2]), .Cout(one_bit_adder_3_cout));
  one_bit_adder one_bit_adder_4 (
    .Cin(one_bit_adder_3_cout), .a(A[3]), .b(xor_4_out), .sum(result[3]), .Cout(one_bit_adder_4_cout));
  one_bit_adder one_bit_adder_5 (
    .Cin(one_bit_adder_4_cout), .a(A[4]), .b(xor_5_out), .sum(result[4]), .Cout(one_bit_adder_5_cout));
  one_bit_adder one_bit_adder_6 (
    .Cin(one_bit_adder_5_cout), .a(A[5]), .b(xor_6_out), .sum(result[5]), .Cout(one_bit_adder_6_cout));
  one_bit_adder one_bit_adder_7 (
    .Cin(one_bit_adder_6_cout), .a(A[6]), .b(xor_7_out), .sum(result[6]), .Cout(one_bit_adder_7_cout));
  one_bit_adder one_bit_adder_8 (
    .Cin(one_bit_adder_7_cout), .a(A[7]), .b(xor_8_out), .sum(result[7]), .Cout(one_bit_adder_8_cout));
  one_bit_adder one_bit_adder_9 (
    .Cin(one_bit_adder_8_cout), .a(A[8]), .b(xor_9_out), .sum(result[8]), .Cout(one_bit_adder_9_cout));
  one_bit_adder one_bit_adder_10 (
    .Cin(one_bit_adder_9_cout), .a(A[9]), .b(xor_10_out), .sum(result[9]), .Cout(one_bit_adder_10_cout));
  one_bit_adder one_bit_adder_11 (
    .Cin(one_bit_adder_10_cout), .a(A[10]), .b(xor_11_out), .sum(result[10]), .Cout(one_bit_adder_11_cout));
  one_bit_adder one_bit_adder_12 (
    .Cin(one_bit_adder_11_cout), .a(A[11]), .b(xor_12_out), .sum(result[11]), .Cout(one_bit_adder_12_cout));
  one_bit_adder one_bit_adder_13 (
    .Cin(one_bit_adder_12_cout), .a(A[12]), .b(xor_13_out), .sum(result[12]), .Cout(one_bit_adder_13_cout));
  one_bit_adder one_bit_adder_14 (
    .Cin(one_bit_adder_13_cout), .a(A[13]), .b(xor_14_out), .sum(result[13]), .Cout(one_bit_adder_14_cout));
  one_bit_adder one_bit_adder_15 (
    .Cin(one_bit_adder_14_cout), .a(A[14]), .b(xor_15_out), .sum(result[14]), .Cout(one_bit_adder_15_cout));
  one_bit_adder one_bit_adder_16 (
    .Cin(one_bit_adder_15_cout), .a(A[15]), .b(xor_16_out), .sum(result[15]), .Cout(one_bit_adder_16_cout));
  xor xor_17 (ovf, one_bit_adder_15_cout, one_bit_adder_16_cout);
endmodule

module one_bit_adder (
  input  Cin,
  input  a,
  input  b,
  output sum,
  output Cout
);

  wire and_1_out, and_2_out, xor_1_out;

  xor xor_1 (xor_1_out, a, b);
  xor xor_2 (sum, xor_1_out, Cin);
  and and_1 (and_1_out, Cin, xor_1_out);
  and and_2 (and_2_out, b, a);
  or or_1 (Cout, and_1_out, and_2_out);
endmodule
